// Logisim project MIPS_CPU.circ as structural Verilog
module main (
  input  enable,
  input  clear
);

  wire clock_out, registerfile_1_p6;
  wire [4:0] IA_rd, IA_rs, IA_rt, IA_shamt, multiplexer_3_out, multiplexer_4_out, multiplexer_5_out;
  wire [15:0] AddM_output, IA_immi1, shifter_2_out;
  wire [23:0] adder_1_out, bit_extender_5_out, bit_extender_6_out, bit_extender_7_out, bit_extender_8_out,
       multiplexer_1_out, NPC_out_5, PC_q;
  wire [25:0] IA_immi2, shifter_3_out;
  wire [31:0] alu_1_p3, alu_1_p4, bit_extender_1_out, bit_extender_2_out, bit_extender_3_out,
       bit_extender_4_out, DM_out_7, multiplexer_2_out, multiplexer_6_out, registerfile_1_p7, rom_1_data,
       shifter_1_out;

  Clock clock (.out(clock_out));
  Multiplexer #(.select(2), .width(24), .disabled(0)) multiplexer_1 (
    .in0(24'h4), .in1(bit_extender_5_out), .in2(bit_extender_7_out), .in3(bit_extender_6_out),
    .out(multiplexer_1_out), .en(enable));  // open: sel
  NPC NPC (.offset(multiplexer_1_out), .PC(PC_q), .enable(enable), .out_5(NPC_out_5));  // open: branch
  Register #(.width(24)) PC (.D(NPC_out_5), .en(enable), .Q(PC_q), .clk(clock_out), .clr(clear));
  AddModifier AddM (.address(PC_q), .\output (AddM_output));
  assign bit_extender_1_out = {{16{1'b0}}, IA_immi1};  // Bit_Extender bit_extender_1
  assign bit_extender_2_out = {{8{1'b0}}, adder_1_out};  // Bit_Extender bit_extender_2
  Adder #(.width(24)) adder_1 (.a(PC_q), .b(24'h8), .out(adder_1_out));  // open: cin, cout
  Shifter #(.width(32)) shifter_1 (.in(bit_extender_1_out), .\dist (5'b10000), .out(shifter_1_out));
  ROM #(.addrWidth(16), .dataWidth(32)) rom_1 (.addr(AddM_output), .data(rom_1_data));  // open: sel
  IA IA (
    .instruction(rom_1_data), .Rs(IA_rs), .Rt(IA_rt), .Rd(IA_rd), .shamt(IA_shamt), .immi1(IA_immi1),
    .immi2(IA_immi2), .in_3(enable));  // open: size, op, funct
  assign bit_extender_3_out = {{16{1'b0}}, IA_immi1};  // Bit_Extender bit_extender_3
  assign bit_extender_4_out = {{27{1'b0}}, IA_shamt};  // Bit_Extender bit_extender_4
  Shifter #(.width(16)) shifter_2 (.in(IA_immi1), .\dist (4'b0010), .out(shifter_2_out));
  Multiplexer #(.select(2), .width(32)) multiplexer_2 (
    .in0(alu_1_p3), .in1(DM_out_7), .in2(bit_extender_2_out), .in3(shifter_1_out), .out(multiplexer_2_out),
    .en(enable));  // open: sel
  assign bit_extender_5_out = {{8{1'b0}}, shifter_2_out};  // Bit_Extender bit_extender_5
  Shifter #(.width(26)) shifter_3 (.in(IA_immi2), .\dist (5'b00010), .out(shifter_3_out));
  Multiplexer #(.select(2), .width(5)) multiplexer_3 (
    .in0(IA_rd), .in1(IA_rt), .in2({5{1'b1}}), .in3({5{1'b0}}), .out(multiplexer_3_out), .en(enable));  // open: sel
  Multiplexer #(.select(2), .width(5)) multiplexer_4 (
    .in0(IA_rs), .in1(IA_rt), .in2(5'b00010), .in3({5{1'b0}}), .out(multiplexer_4_out), .en(enable));  // open: sel
  Bit_Extender #(.in_width(26), .out_width(24)) bit_extender_6 (.in(shifter_3_out), .out(bit_extender_6_out));
  Multiplexer #(.width(5)) multiplexer_5 (
    .in0(IA_rt), .in1({5{1'b0}}), .out(multiplexer_5_out), .en(enable));  // open: sel
  // RegisterFile registerfile_1: pin names not known; wires that end beside it: multiplexer_2_out, clock_out, multiplexer_3_out, multiplexer_4_out, multiplexer_5_out, registerfile_1_p6, registerfile_1_p7
  Multiplexer #(.select(2), .width(32)) multiplexer_6 (
    .in0(registerfile_1_p7), .in1(bit_extender_3_out), .in2(bit_extender_4_out), .in3(32'ha),
    .out(multiplexer_6_out), .en(enable));  // open: sel
  Bit_Extender #(.in_width(32), .out_width(24)) bit_extender_7 (.in(registerfile_1_p7), .out(bit_extender_7_out));
  // ALU alu_1: pin names not known; wires that end beside it: registerfile_1_p6, multiplexer_6_out, alu_1_p3, alu_1_p4
  Bit_Extender #(.in_width(32), .out_width(24)) bit_extender_8 (.in(alu_1_p3), .out(bit_extender_8_out));
  DM DM (
    .in_1(alu_1_p4), .address(bit_extender_8_out), .enable(enable), .clock(clock_out), .clear(clear),
    .out_7(DM_out_7));  // open: store
endmodule

module IA (
  input  [31:0] instruction,
  input  [1:0] size,
  input  in_3,
  output [5:0] op,
  output [4:0] Rs,
  output [4:0] Rt,
  output [4:0] Rd,
  output [4:0] shamt,
  output [5:0] funct,
  output [15:0] immi1,
  output [25:0] immi2
);

  Multiplexer #(.select(2), .width(5), .disabled(0)) multiplexer_1 (
    .in0(instruction[10:6]), .in1(instruction[10:6]), .in2(instruction[20:16]), .in3(instruction[20:16]),
    .out(Rs), .sel(size), .en(in_3));
  Multiplexer #(.select(2), .width(5), .disabled(0)) multiplexer_2 (
    .in0(instruction[15:11]), .in1(instruction[15:11]), .in2(instruction[20:16]), .in3(instruction[20:16]),
    .out(Rt), .sel(size), .en(in_3));
  Multiplexer #(.select(2), .width(5), .disabled(0)) multiplexer_3 (
    .in0(instruction[20:16]), .in1(instruction[20:16]), .in2(instruction[20:16]), .in3(instruction[20:16]),
    .out(Rd), .sel(size), .en(in_3));
  Multiplexer #(.select(2), .width(5), .disabled(0)) multiplexer_4 (
    .in0(instruction[25:21]), .in1(instruction[20:16]), .in2(instruction[20:16]), .in3(instruction[20:16]),
    .out(shamt), .sel(size), .en(in_3));
  Multiplexer #(.select(2), .width(6), .disabled(0)) multiplexer_5 (
    .in0(instruction[31:26]), .in1({6{1'b0}}), .in2({6{1'b0}}), .in3({6{1'b0}}), .out(funct), .sel(size),
    .en(in_3));
  Multiplexer #(.select(2), .width(16), .disabled(0)) multiplexer_6 (
    .in0({16{1'b0}}), .in1(instruction[31:16]), .in2({16{1'b0}}), .in3({16{1'b0}}), .out(immi1), .sel(size),
    .en(in_3));
  Multiplexer #(.select(2), .width(26), .disabled(0)) multiplexer_7 (
    .in0({26{1'b0}}), .in1({26{1'b0}}), .in2(instruction[31:6]), .in3({26{1'b0}}), .out(immi2), .sel(size),
    .en(in_3));

  assign op = instruction[5:0];
  // also tied to GND on the sheet: {instruction[16], instruction[17], instruction[18], instruction[19], instruction[20]}
endmodule

module DM (
  input  [31:0] in_1,
  input  [23:0] address,
  input  store,
  input  enable,
  input  clock,
  input  clear,
  output [31:0] out_7
);

  RAM #(.addrWidth(24), .dataWidth(32), .bus("separate")) ram_1 (
    .addr(address), .din(in_1), .data(out_7), .str(store), .sel(enable), .clk(clock), .ld(1'b1), .clr(clear));
endmodule

module NPC (
  input  [23:0] offset,
  input  [23:0] PC,
  input  branch,
  input  enable,
  output [23:0] out_5
);

  wire [23:0] multiplexer_1_out;

  Multiplexer #(.width(24)) multiplexer_1 (
    .in0(24'h4), .in1(offset), .out(multiplexer_1_out), .sel(branch), .en(enable));
  Adder #(.width(24)) adder_1 (.a(multiplexer_1_out), .b(PC), .out(out_5));  // open: cin, cout
endmodule

module AddModifier (
  input  [23:0] address,
  output [15:0] \output 
);

  wire [23:0] shifter_1_out;

  Shifter #(.width(24), .shift("lr")) shifter_1 (.in(address), .\dist (5'b00010), .out(shifter_1_out));
  Bit_Extender #(.in_width(24)) bit_extender_1 (.in(shifter_1_out), .out(\output ));
endmodule

module CO (
  input  [5:0] OP,
  input  [5:0] FUN,
  output [1:0] SIZE,
  output [1:0] R1_num,
  output R2_num,
  output [1:0] W_num,
  output [1:0] RFin,
  output [1:0] ALUb,
  output [1:0] NPC
);

  wire Add, AddI, AddIU, AddU, And, and_1_out, and_3_out, and_6_out, and_7_out, and_8_out, and_9_out,
       and_13_out, and_14_out, and_15_out, and_16_out, and_17_out, and_18_out, and_22_out, and_23_out,
       and_24_out, and_25_out, and_26_out, and_27_out, and_36_out, and_37_out, and_38_out, and_39_out,
       and_40_out, and_41_out, and_48_out, and_50_out, ANDI, BEQ, BLTZ, BNE, JAL, JR, JUMP, LH, LOADW, LUI,
       NOR, OR, ORI, SLL, SLT, SLTI, SLTU, SRA, SRL, STOREW, SUB, SYS, XORI;

  and and_1 (and_1_out, ~OP[0], ~OP[1], ~OP[2], ~OP[3], ~OP[4], ~OP[5]);  // AND_Gate
  and and_2 (Add, and_1_out, and_3_out);
  and and_3 (and_3_out, ~FUN[0], ~FUN[1], ~FUN[2], ~FUN[3], ~FUN[4], FUN[5]);  // AND_Gate
  and and_4 (AddI, ~OP[0], ~OP[1], ~OP[2], OP[3], ~OP[4], ~OP[5]);  // AND_Gate
  and and_5 (AddIU, OP[0], ~OP[1], ~OP[2], OP[3], ~OP[4], ~OP[5]);  // AND_Gate
  and and_6 (and_6_out, ~OP[0], ~OP[1], ~OP[2], ~OP[3], ~OP[4], ~OP[5]);  // AND_Gate
  and and_7 (and_7_out, FUN[0], ~FUN[1], ~FUN[2], ~FUN[3], ~FUN[4], FUN[5]);  // AND_Gate
  and and_8 (and_8_out, ~OP[0], ~OP[1], ~OP[2], ~OP[3], ~OP[4], ~OP[5]);  // AND_Gate
  and and_9 (and_9_out, ~FUN[0], ~FUN[1], FUN[2], ~FUN[3], ~FUN[4], FUN[5]);  // AND_Gate
  and and_10 (ANDI, ~OP[0], ~OP[1], OP[2], OP[3], ~OP[4], ~OP[5]);  // AND_Gate
  and and_11 (AddU, and_6_out, and_7_out);
  and and_12 (And, and_8_out, and_9_out);
  and and_13 (and_13_out, ~OP[0], ~OP[1], ~OP[2], ~OP[3], ~OP[4], ~OP[5]);  // AND_Gate
  and and_14 (and_14_out, FUN[0], FUN[1], ~FUN[2], ~FUN[3], ~FUN[4], ~FUN[5]);  // AND_Gate
  and and_15 (and_15_out, ~OP[0], ~OP[1], ~OP[2], ~OP[3], ~OP[4], ~OP[5]);  // AND_Gate
  and and_16 (and_16_out, ~FUN[0], FUN[1], ~FUN[2], ~FUN[3], ~FUN[4], ~FUN[5]);  // AND_Gate
  and and_17 (and_17_out, ~OP[0], ~OP[1], ~OP[2], ~OP[3], ~OP[4], ~OP[5]);  // AND_Gate
  and and_18 (and_18_out, ~FUN[0], ~FUN[1], ~FUN[2], ~FUN[3], ~FUN[4], ~FUN[5]);  // AND_Gate
  and and_19 (SRA, and_13_out, and_14_out);
  and and_20 (SRL, and_15_out, and_16_out);
  and and_21 (SLL, and_17_out, and_18_out);
  and and_22 (and_22_out, ~OP[0], ~OP[1], ~OP[2], ~OP[3], ~OP[4], ~OP[5]);  // AND_Gate
  and and_23 (and_23_out, ~FUN[0], FUN[1], ~FUN[2], ~FUN[3], ~FUN[4], FUN[5]);  // AND_Gate
  and and_24 (and_24_out, ~OP[0], ~OP[1], ~OP[2], ~OP[3], ~OP[4], ~OP[5]);  // AND_Gate
  and and_25 (and_25_out, FUN[0], ~FUN[1], FUN[2], ~FUN[3], ~FUN[4], FUN[5]);  // AND_Gate
  and and_26 (and_26_out, ~OP[0], ~OP[1], ~OP[2], ~OP[3], ~OP[4], ~OP[5]);  // AND_Gate
  and and_27 (and_27_out, FUN[0], FUN[1], FUN[2], ~FUN[3], ~FUN[4], FUN[5]);  // AND_Gate
  and and_28 (SUB, and_22_out, and_23_out);
  and and_29 (OR, and_24_out, and_25_out);
  and and_30 (NOR, and_26_out, and_27_out);
  and and_31 (ORI, OP[0], ~OP[1], OP[2], OP[3], ~OP[4], ~OP[5]);  // AND_Gate
  and and_32 (LOADW, OP[0], OP[1], ~OP[2], ~OP[3], ~OP[4], OP[5]);  // AND_Gate
  and and_33 (STOREW, OP[0], OP[1], ~OP[2], OP[3], ~OP[4], OP[5]);  // AND_Gate
  and and_34 (BEQ, ~OP[0], ~OP[1], OP[2], ~OP[3], ~OP[4], ~OP[5]);  // AND_Gate
  and and_35 (BNE, OP[0], ~OP[1], OP[2], ~OP[3], ~OP[4], ~OP[5]);  // AND_Gate
  and and_36 (and_36_out, ~OP[0], ~OP[1], ~OP[2], ~OP[3], ~OP[4], ~OP[5]);  // AND_Gate
  and and_37 (and_37_out, ~FUN[0], FUN[1], ~FUN[2], FUN[3], ~FUN[4], FUN[5]);  // AND_Gate
  and and_38 (and_38_out, ~OP[0], ~OP[1], ~OP[2], ~OP[3], ~OP[4], ~OP[5]);  // AND_Gate
  and and_39 (and_39_out, FUN[0], FUN[1], ~FUN[2], FUN[3], ~FUN[4], FUN[5]);  // AND_Gate
  and and_40 (and_40_out, ~OP[0], ~OP[1], ~OP[2], ~OP[3], ~OP[4], ~OP[5]);  // AND_Gate
  and and_41 (and_41_out, ~FUN[0], ~FUN[1], ~FUN[2], FUN[3], ~FUN[4], ~FUN[5]);  // AND_Gate
  and and_42 (SLT, and_36_out, and_37_out);
  and and_43 (SLTU, and_38_out, and_39_out);
  and and_44 (JR, and_40_out, and_41_out);
  and and_45 (SLTI, OP[0], ~OP[1], OP[2], OP[3], ~OP[4], ~OP[5]);  // AND_Gate
  and and_46 (JUMP, ~OP[0], OP[1], ~OP[2], ~OP[3], ~OP[4], ~OP[5]);  // AND_Gate
  and and_47 (JAL, OP[0], OP[1], ~OP[2], ~OP[3], ~OP[4], ~OP[5]);  // AND_Gate
  and and_48 (and_48_out, ~OP[0], ~OP[1], ~OP[2], ~OP[3], ~OP[4], ~OP[5]);  // AND_Gate
  and and_49 (SYS, and_48_out, and_50_out);
  and and_50 (and_50_out, ~FUN[0], ~FUN[1], FUN[2], FUN[3], ~FUN[4], ~FUN[5]);  // AND_Gate
  and and_51 (XORI, ~OP[0], OP[1], OP[2], OP[3], ~OP[4], ~OP[5]);  // AND_Gate
  and and_52 (LUI, OP[0], OP[1], OP[2], OP[3], ~OP[4], ~OP[5]);  // AND_Gate
  and and_53 (LH, OP[0], ~OP[1], ~OP[2], ~OP[3], ~OP[4], OP[5]);  // AND_Gate
  and and_54 (BLTZ, OP[0], ~OP[1], ~OP[2], ~OP[3], ~OP[4], ~OP[5]);  // AND_Gate

  // Notes on the sheet:
  //   AddI(1000)
  //   AddIU(1001)
  //   Add(100000)
  //   AddU(100001)
  //   And(100100)
  //   ANDI(1100)
  //   SRA(11)
  //   SRL(10)
  //   SLL(0)
  //   SUB(100010)
  //   OR(100101)
  //   NOR(100111)
  //   ORI(1101)
  //   LOADW(100011)
  //   STOREW(101011)
  //   BEQ(100)
  //   BNE(101)
  //   SLT(101010)
  //   SLTU(101011)
  //   JR(1000)
  //   SLTI(1010)
  //   JUMP(10)
  //   JAL(11)
  //   SYS(1100)
  //   XORI(1110)
  //   LUI(1111)
  //   LH(100001)
  //   BLTZ(1)
endmodule
